// Logisim project counter.circ as structural Verilog: 4 circuits, main circuit RSasync
module RSasync (
  input  R,
  input  S,
  output Q,
  output notQ
);

  wire or_1_out, or_2_out, por_1_out;

  POR #(.PorHighDuration(1)) por_1 (.out(por_1_out));
  or or_1 (or_1_out, R, por_1_out);
  buf or_2 (or_2_out, S);  // OR_Gate
  nor nor_1 (Q, or_1_out, notQ);
  nor nor_2 (notQ, Q, or_2_out);
endmodule

module RSsync (
  input  R,
  input  C,
  input  S,
  output Q,
  output notQ
);

  wire and_1_out, and_2_out;

  and and_1 (and_1_out, R, C);
  and and_2 (and_2_out, C, S);
  RSasync rsasync_1 (.R(and_1_out), .S(and_2_out), .Q(Q), .notQ(notQ));
endmodule

module JK (
  input  K,
  input  C,
  input  J,
  output Q,
  output notQ
);

  wire and_1_out, and_2_out, not_1_out, rssync_1_notq, rssync_1_q;

  and and_1 (and_1_out, Q, K);
  and and_2 (and_2_out, J, notQ);
  not not_1 (not_1_out, C);
  RSsync rssync_1 (.R(and_1_out), .C(C), .S(and_2_out), .Q(rssync_1_q), .notQ(rssync_1_notq));
  RSsync rssync_2 (.R(rssync_1_notq), .C(not_1_out), .S(rssync_1_q), .Q(Q), .notQ(notQ));
endmodule

module main (
  input  B,
  output Q0,
  output Q1,
  output Q2,
  output Q3
);

  wire and_1_out, and_2_out, and_3_out, jk_1_notq, jk_1_q, jk_2_notq, jk_3_notq, jk_3_q, jk_4_notq, jk_4_q,
       nand_1_out, not_1_out, not_2_out, not_3_out, not_4_out, not_5_out, not_6_out;

  not not_1 (not_1_out, and_3_out);
  and and_1 (and_1_out, jk_2_notq, not_1_out);
  and and_2 (and_2_out, not_1_out, jk_3_notq);
  JK jk_1 (.K(jk_1_q), .C(jk_4_notq), .J(jk_1_notq), .Q(jk_1_q), .notQ(jk_1_notq));
  JK jk_2 (.K(Q0), .C(B), .J(jk_2_notq), .Q(Q0), .notQ(jk_2_notq));
  JK jk_3 (.K(jk_3_q), .C(and_1_out), .J(and_2_out), .Q(jk_3_q), .notQ(jk_3_notq));
  JK jk_4 (.K(jk_4_q), .C(jk_3_notq), .J(jk_4_notq), .Q(jk_4_q), .notQ(jk_4_notq));
  not not_2 (not_2_out, jk_1_q);
  not not_3 (not_3_out, jk_4_q);
  and and_3 (and_3_out, B, not_2_out, not_3_out, not_4_out, not_5_out);
  not not_4 (not_4_out, jk_3_q);
  not not_5 (not_5_out, Q0);
  not not_6 (not_6_out, Q0);
  and and_4 (Q1, jk_3_q, nand_1_out);
  nand nand_1 (nand_1_out, not_6_out, jk_3_q, jk_4_q, jk_1_q);
  and and_5 (Q2, nand_1_out, jk_4_q);
  and and_6 (Q3, nand_1_out, jk_1_q);

  // Notes on the sheet:
  //   Подождите 2-3 секунды перед использованием схемы, чтобы POR успел совершить свою работу.
endmodule
