// Logisim project lsfr.circ as structural Verilog: 4 circuits, main circuit DFront1
module DFront1 (
  input  SET,
  input  D,
  input  C,
  input  RESET,
  output Q,
  output notQ
);

  wire dfront0_1_q, not_1_out;

  not not_1 (not_1_out, C);
  DFront0 dfront0_1 (.SET(SET), .D(D), .C(C), .RESET(RESET), .Q(dfront0_1_q));  // open: notQ
  DFront0 dfront0_2 (.D(dfront0_1_q), .C(not_1_out), .Q(Q), .notQ(notQ));  // open: SET, RESET
endmodule

module main (
  input  Init,
  input  SetReset13,
  input  SetReset12,
  input  SetReset11,
  input  SetReset10,
  input  SetReset9,
  input  SetReset8,
  input  SetReset7,
  input  SetReset6,
  input  SetReset5,
  input  SetReset4,
  input  SetReset3,
  input  SetReset2,
  input  SetReset1,
  input  SetReset0,
  input  B,
  output Q13,
  output Q12,
  output Q11,
  output Q10,
  output Q9,
  output Q8,
  output Q7,
  output Q6,
  output Q5,
  output Q4,
  output Q3,
  output Q2,
  output Q1,
  output Q0
);

  wire I0_reset, I0_set, I1_reset, I1_set, I2_reset, I2_set, I3_reset, I3_set, I4_reset, I4_set, I5_reset,
       I5_set, I6_reset, I6_set, I7_reset, I7_set, I8_reset, I8_set, I9_reset, I9_set, I10_reset, I10_set,
       I11_reset, I11_set, I12_reset, I12_set, I13_reset, I13_set, xor_1_out;

  InitHelper I13 (.init(Init), .value(SetReset13), .Set(I13_set), .Reset(I13_reset));
  InitHelper I10 (.init(Init), .value(SetReset10), .Set(I10_set), .Reset(I10_reset));
  InitHelper I7 (.init(Init), .value(SetReset7), .Set(I7_set), .Reset(I7_reset));
  InitHelper I4 (.init(Init), .value(SetReset4), .Set(I4_set), .Reset(I4_reset));
  InitHelper I1 (.init(Init), .value(SetReset1), .Set(I1_set), .Reset(I1_reset));
  DFront1 D13 (.SET(I13_set), .D(xor_1_out), .C(B), .RESET(I13_reset), .Q(Q13));  // open: notQ
  DFront1 D10 (.SET(I10_set), .D(Q11), .C(B), .RESET(I10_reset), .Q(Q10));  // open: notQ
  DFront1 D7 (.SET(I7_set), .D(Q8), .C(B), .RESET(I7_reset), .Q(Q7));  // open: notQ
  DFront1 D4 (.SET(I4_set), .D(Q5), .C(B), .RESET(I4_reset), .Q(Q4));  // open: notQ
  DFront1 D1 (.SET(I1_set), .D(Q2), .C(B), .RESET(I1_reset), .Q(Q1));  // open: notQ
  InitHelper I12 (.init(Init), .value(SetReset12), .Set(I12_set), .Reset(I12_reset));
  InitHelper I9 (.init(Init), .value(SetReset9), .Set(I9_set), .Reset(I9_reset));
  InitHelper I6 (.init(Init), .value(SetReset6), .Set(I6_set), .Reset(I6_reset));
  InitHelper I3 (.init(Init), .value(SetReset3), .Set(I3_set), .Reset(I3_reset));
  InitHelper I0 (.init(Init), .value(SetReset0), .Set(I0_set), .Reset(I0_reset));
  DFront1 D12 (.SET(I12_set), .D(Q13), .C(B), .RESET(I12_reset), .Q(Q12));  // open: notQ
  DFront1 D9 (.SET(I9_set), .D(Q10), .C(B), .RESET(I9_reset), .Q(Q9));  // open: notQ
  DFront1 D6 (.SET(I6_set), .D(Q7), .C(B), .RESET(I6_reset), .Q(Q6));  // open: notQ
  DFront1 D3 (.SET(I3_set), .D(Q4), .C(B), .RESET(I3_reset), .Q(Q3));  // open: notQ
  DFront1 D0 (.SET(I0_set), .D(Q1), .C(B), .RESET(I0_reset), .Q(Q0));  // open: notQ
  InitHelper I11 (.init(Init), .value(SetReset11), .Set(I11_set), .Reset(I11_reset));
  InitHelper I8 (.init(Init), .value(SetReset8), .Set(I8_set), .Reset(I8_reset));
  InitHelper I5 (.init(Init), .value(SetReset5), .Set(I5_set), .Reset(I5_reset));
  InitHelper I2 (.init(Init), .value(SetReset2), .Set(I2_set), .Reset(I2_reset));
  DFront1 D11 (.SET(I11_set), .D(Q12), .C(B), .RESET(I11_reset), .Q(Q11));  // open: notQ
  DFront1 D8 (.SET(I8_set), .D(Q9), .C(B), .RESET(I8_reset), .Q(Q8));  // open: notQ
  DFront1 D5 (.SET(I5_set), .D(Q6), .C(B), .RESET(I5_reset), .Q(Q5));  // open: notQ
  DFront1 D2 (.SET(I2_set), .D(Q3), .C(B), .RESET(I2_reset), .Q(Q2));  // open: notQ
  xor xor_1 (xor_1_out, Q0, Q8, Q11, Q12, Q13);
endmodule

module InitHelper (
  input  init,
  input  value,
  output Set,
  output Reset
);

  wire not_1_out;

  and and_1 (Set, init, value);
  not not_1 (not_1_out, value);
  and and_2 (Reset, not_1_out, init);
endmodule

module DFront0 (
  input  SET,
  input  D,
  input  C,
  input  RESET,
  output Q,
  output notQ
);

  wire nand_1_out, nand_2_out, nand_3_out, nand_4_out, por_1_out;

  nand nand_1 (nand_1_out, D, C);
  nand nand_2 (nand_2_out, nand_1_out, C);
  POR por_1 (.out(por_1_out));
  nand nand_3 (nand_3_out, nand_1_out, notQ);
  nand nand_4 (nand_4_out, Q, nand_2_out);
  or or_1 (Q, SET, nand_3_out);
  or or_2 (notQ, nand_4_out, por_1_out, RESET);
endmodule
