// Logisim project counter.circ as structural Verilog: 3 circuits, main circuit main
module main (
  input  C,
  output Q0,
  output Q1,
  output Q2,
  output Q3
);

  wire and_1_out, not_1_out, or_1_out, or_2_out;

  not not_1 (not_1_out, Q3);
  T_Trigger t_trigger_1 (.T(C), .C(not_1_out), .Q(Q0));
  T_Trigger t_trigger_2 (.T(Q0), .C(not_1_out), .Q(Q1));
  and and_1 (and_1_out, C, Q3);
  T_Trigger t_trigger_3 (.T(Q1), .C(not_1_out), .Q(Q2));
  or or_1 (or_1_out, and_1_out, not_1_out);
  or or_2 (or_2_out, Q2, and_1_out);
  T_Trigger t_trigger_4 (.T(or_2_out), .C(or_1_out), .Q(Q3));
endmodule

module D_Trigger (
  input  D,
  input  C,
  output Q,
  output NQ
);

  wire nand_1_out, nand_2_out, nand_4_out, por_1_out;

  nand nand_1 (nand_1_out, D, C);
  nand nand_2 (nand_2_out, nand_1_out, C);
  nand nand_3 (Q, nand_1_out, NQ);
  nand nand_4 (nand_4_out, Q, nand_2_out);
  POR por_1 (.out(por_1_out));
  or or_1 (NQ, nand_4_out, por_1_out);
endmodule

module T_Trigger (
  input  T,
  input  C,
  output Q
);

  wire and_1_out, d_trigger_1_q, d_trigger_2_nq, not_1_out;

  and and_1 (and_1_out, T, C);
  not not_1 (not_1_out, and_1_out);
  D_Trigger d_trigger_1 (.D(d_trigger_2_nq), .C(and_1_out), .Q(d_trigger_1_q));  // open: NQ
  D_Trigger d_trigger_2 (.D(d_trigger_1_q), .C(not_1_out), .Q(Q), .NQ(d_trigger_2_nq));
endmodule
