// Logisim project lfsr.circ as structural Verilog: 3 circuits, main circuit main
module main (
  input  C,
  input  I,
  input  A0,
  input  A1,
  input  A2,
  input  A3,
  input  A4,
  input  A5,
  input  A6,
  input  A7,
  input  A8,
  input  A9,
  input  A10,
  input  A11,
  input  A12,
  input  A13,
  input  A14,
  input  A15,
  output Q0,
  output Q1,
  output Q2,
  output Q3,
  output Q4,
  output Q5,
  output Q6,
  output Q7,
  output Q8,
  output Q9,
  output Q10,
  output Q11,
  output Q12,
  output Q13,
  output Q14,
  output Q15
);

  wire and_1_out, and_2_out, and_3_out, and_4_out, and_5_out, and_6_out, and_7_out, and_8_out, and_9_out,
       and_10_out, and_11_out, and_12_out, and_13_out, and_14_out, and_15_out, and_16_out, or_1_out,
       or_2_out, or_3_out, or_4_out, or_5_out, or_6_out, or_7_out, or_8_out, or_9_out, or_10_out, or_11_out,
       or_12_out, or_13_out, or_14_out, or_15_out, or_16_out, or_17_out, xor_1_out, xor_2_out;

  xor xor_1 (xor_1_out, Q7, Q15);
  or or_1 (or_1_out, C, I);
  xor xor_2 (xor_2_out, xor_1_out, Q0);
  or or_2 (or_2_out, Q7, and_9_out);
  or or_3 (or_3_out, xor_2_out, and_1_out);
  and and_1 (and_1_out, I, A0);
  and and_2 (and_2_out, I, A1);
  and and_3 (and_3_out, I, A2);
  and and_4 (and_4_out, I, A3);
  and and_5 (and_5_out, I, A4);
  and and_6 (and_6_out, I, A5);
  and and_7 (and_7_out, I, A6);
  and and_8 (and_8_out, I, A7);
  and and_9 (and_9_out, I, A8);
  and and_10 (and_10_out, I, A9);
  and and_11 (and_11_out, I, A10);
  and and_12 (and_12_out, I, A11);
  and and_13 (and_13_out, I, A12);
  and and_14 (and_14_out, I, A13);
  and and_15 (and_15_out, I, A14);
  and and_16 (and_16_out, I, A15);
  D_Trigger_Front d_trigger_front_1 (.D(or_3_out), .C(or_1_out), .Q(Q0));  // open: NQ
  D_Trigger_Front d_trigger_front_2 (.D(or_2_out), .C(or_1_out), .Q(Q8));  // open: NQ
  or or_4 (or_4_out, Q0, and_2_out);
  or or_5 (or_5_out, and_10_out, Q8);
  D_Trigger_Front d_trigger_front_3 (.D(or_4_out), .C(or_1_out), .Q(Q1));  // open: NQ
  D_Trigger_Front d_trigger_front_4 (.D(or_5_out), .C(or_1_out), .Q(Q9));  // open: NQ
  or or_6 (or_6_out, Q1, and_3_out);
  or or_7 (or_7_out, Q9, and_11_out);
  D_Trigger_Front d_trigger_front_5 (.D(or_6_out), .C(or_1_out), .Q(Q2));  // open: NQ
  D_Trigger_Front d_trigger_front_6 (.D(or_7_out), .C(or_1_out), .Q(Q10));  // open: NQ
  or or_8 (or_8_out, Q2, and_4_out);
  or or_9 (or_9_out, Q10, and_12_out);
  or or_10 (or_10_out, Q3, and_5_out);
  D_Trigger_Front d_trigger_front_7 (.D(or_8_out), .C(or_1_out), .Q(Q3));  // open: NQ
  D_Trigger_Front d_trigger_front_8 (.D(or_9_out), .C(or_1_out), .Q(Q11));  // open: NQ
  or or_11 (or_11_out, Q11, and_13_out);
  or or_12 (or_12_out, Q4, and_6_out);
  D_Trigger_Front d_trigger_front_9 (.D(or_10_out), .C(or_1_out), .Q(Q4));  // open: NQ
  D_Trigger_Front d_trigger_front_10 (.D(or_11_out), .C(or_1_out), .Q(Q12));  // open: NQ
  or or_13 (or_13_out, Q12, and_14_out);
  or or_14 (or_14_out, Q5, and_7_out);
  D_Trigger_Front d_trigger_front_11 (.D(or_12_out), .C(or_1_out), .Q(Q5));  // open: NQ
  D_Trigger_Front d_trigger_front_12 (.D(or_13_out), .C(or_1_out), .Q(Q13));  // open: NQ
  or or_15 (or_15_out, Q13, and_15_out);
  D_Trigger_Front d_trigger_front_13 (.D(or_14_out), .C(or_1_out), .Q(Q6));  // open: NQ
  D_Trigger_Front d_trigger_front_14 (.D(or_15_out), .C(or_1_out), .Q(Q14));  // open: NQ
  buf or_16 (or_16_out, Q6);  // OR_Gate
  or or_17 (or_17_out, Q14, and_16_out);
  D_Trigger_Front d_trigger_front_15 (.D(or_16_out), .C(or_1_out), .Q(Q7));  // open: NQ
  D_Trigger_Front d_trigger_front_16 (.D(or_17_out), .C(or_1_out), .Q(Q15));  // open: NQ
endmodule

module D_Trigger (
  input  D,
  input  C,
  output Q,
  output NQ
);

  wire nand_1_out, nand_2_out, nand_4_out, por_1_out;

  nand nand_1 (nand_1_out, D, C);
  nand nand_2 (nand_2_out, nand_1_out, C);
  nand nand_3 (Q, nand_1_out, NQ);
  nand nand_4 (nand_4_out, Q, nand_2_out);
  POR por_1 (.out(por_1_out));
  or or_1 (NQ, nand_4_out, por_1_out);
endmodule

module D_Trigger_Front (
  input  D,
  input  C,
  output Q,
  output NQ
);

  wire d_trigger_1_q, not_1_out;

  not not_1 (not_1_out, C);
  D_Trigger d_trigger_1 (.D(D), .C(C), .Q(d_trigger_1_q));  // open: NQ
  D_Trigger d_trigger_2 (.D(d_trigger_1_q), .C(not_1_out), .Q(Q), .NQ(NQ));
endmodule
