// Logisim project MyCounter.circ as structural Verilog: 6 circuits, main circuit main
module main (
  input  C,
  output Q0,
  output Q1,
  output Q2,
  output Q3
);

  wire nor_1_out, nor_2_out, nor_3_out, nor_4_out, not_1_out;

  not not_1 (not_1_out, Q3);
  nor nor_1 (nor_1_out, C, not_1_out);
  TTrigger ttrigger_1 (.C(nor_1_out), .Q(Q0));  // open: NQ
  nor nor_2 (nor_2_out, Q0, not_1_out);
  TTrigger ttrigger_2 (.C(nor_2_out), .Q(Q1));  // open: NQ
  nor nor_3 (nor_3_out, Q1, not_1_out);
  TTrigger ttrigger_3 (.C(nor_3_out), .Q(Q2));  // open: NQ
  nor nor_4 (nor_4_out, Q2, not_1_out);
  TTrigger ttrigger_4 (.C(nor_4_out), .Q(Q3));  // open: NQ
endmodule

module TTrigger (
  input  C,
  output Q,
  output NQ
);

  wire not_1_out, rstriggersync_1_nq, rstriggersync_1_q;

  not not_1 (not_1_out, C);
  RSTriggerSync rstriggersync_1 (.R(NQ), .C(C), .S(Q), .Q(rstriggersync_1_q), .NQ(rstriggersync_1_nq));
  RSTriggerSync rstriggersync_2 (.R(rstriggersync_1_q), .C(not_1_out), .S(rstriggersync_1_nq), .Q(Q), .NQ(NQ));
endmodule

module RSTriggerSync (
  input  R,
  input  C,
  input  S,
  output Q,
  output NQ
);

  wire and_1_out, and_2_out, nor_2_out, por_1_out;

  and and_1 (and_1_out, R, C);
  and and_2 (and_2_out, C, S);
  nor nor_1 (Q, and_1_out, NQ);
  nor nor_2 (nor_2_out, Q, and_2_out);
  POR por_1 (.out(por_1_out));
  or or_1 (NQ, nor_2_out, por_1_out);
endmodule

module TTriggerSync (
  input  T,
  input  C,
  output Q,
  output NQ
);

  wire and_1_out, and_2_out;

  and and_1 (and_1_out, NQ, T);
  and and_2 (and_2_out, T, Q);
  RSTriggerSync rstriggersync_1 (.R(and_1_out), .C(C), .S(and_2_out), .Q(Q), .NQ(NQ));
endmodule

module Test (
  input  C,
  output Q0,
  output Q1,
  output Q2,
  output Q3
);

  TTriggerSync ttriggersync_1 (.T(Q3), .C(C), .Q(Q0));  // open: NQ
  TTriggerSync ttriggersync_2 (.T(Q3), .C(Q0), .Q(Q1));  // open: NQ
  TTriggerSync ttriggersync_3 (.T(Q3), .C(Q1), .Q(Q2));  // open: NQ
  TTriggerSync ttriggersync_4 (.T(Q3), .C(Q2), .Q(Q3));  // open: NQ
endmodule

module JKTrigger (
  input  in_1,
  input  in_2,
  input  in_3,
  output out_4,
  output out_5
);

  wire nand_1_out, nand_2_out, nand_3_out, nand_4_out, or_1_out, or_2_out, por_1_out;

  nand nand_1 (nand_1_out, in_1, in_2);
  nand nand_2 (nand_2_out, in_2, in_3);
  POR por_1 (.out(por_1_out));
  nand nand_3 (nand_3_out, nand_1_out, or_2_out);
  nand nand_4 (nand_4_out, or_1_out, nand_2_out);
  or or_1 (or_1_out, out_4, por_1_out);
  or or_2 (or_2_out, por_1_out, out_5);
  nand nand_5 (out_4, nand_3_out, or_2_out);
  nand nand_6 (out_5, or_1_out, nand_4_out);
endmodule
