// Logisim project counter.circ as structural Verilog: 6 circuits, main circuit main
module main (
  input  C,
  output Q0,
  output Q1,
  output Q2,
  output Q3
);

  wire and_1_out, and_2_out, nor_1_out, not_1_out, not_2_out, or_1_out, or_2_out;

  not not_1 (not_1_out, nor_1_out);
  and and_1 (and_1_out, Q0, Q2, Q2);
  T_Trigger_2 t_trigger_2_1 (.T(C), .C(not_1_out), .Q(Q0));
  T_Trigger_2 t_trigger_2_2 (.T(Q0), .C(not_1_out), .Q(Q1));
  and and_2 (and_2_out, C, nor_1_out);
  T_Trigger_2 t_trigger_2_3 (.T(Q1), .C(not_1_out), .Q(Q2));
  or or_1 (or_1_out, and_2_out, not_1_out);
  or or_2 (or_2_out, Q2, and_2_out);
  not not_2 (not_2_out, Q3);
  T_Trigger_2 t_trigger_2_4 (.T(or_2_out), .C(or_1_out), .Q(Q3));
  nor nor_1 (nor_1_out, not_2_out, and_1_out);
endmodule

module RS_Trigger (
  input  R,
  input  C,
  input  S,
  output Q,
  output NQ
);

  wire and_1_out, and_2_out, nor_2_out, por_1_out;

  and and_1 (and_1_out, R, C);
  and and_2 (and_2_out, C, S);
  POR por_1 (.out(por_1_out));
  nor nor_1 (Q, and_1_out, NQ);
  nor nor_2 (nor_2_out, Q, and_2_out);
  or or_1 (NQ, nor_2_out, por_1_out);
endmodule

module JK_Trigger (
  input  K,
  input  C,
  input  J,
  output Q,
  output NQ
);

  wire and_1_out, and_2_out, not_1_out, rs_trigger_2_nq, rs_trigger_2_q;

  and and_1 (and_1_out, rs_trigger_2_nq, K);
  and and_2 (and_2_out, J, rs_trigger_2_q);
  RS_Trigger rs_trigger_1 (.R(and_1_out), .C(C), .S(and_2_out), .Q(Q), .NQ(NQ));
  not not_1 (not_1_out, C);
  RS_Trigger rs_trigger_2 (.R(Q), .C(not_1_out), .S(NQ), .Q(rs_trigger_2_q), .NQ(rs_trigger_2_nq));
endmodule

module D_Trigger (
  input  D,
  input  C,
  output Q,
  output NQ
);

  wire nand_1_out, nand_2_out, nand_4_out, por_1_out;

  nand nand_1 (nand_1_out, D, C);
  nand nand_2 (nand_2_out, nand_1_out, C);
  nand nand_3 (Q, nand_1_out, NQ);
  nand nand_4 (nand_4_out, Q, nand_2_out);
  POR por_1 (.out(por_1_out));
  or or_1 (NQ, nand_4_out, por_1_out);
endmodule

module T_Trigger_Sync (
  input  T,
  input  C,
  output Q,
  output NQ
);

  wire and_1_out, and_2_out, not_1_out, rs_trigger_1_nq, rs_trigger_1_q;

  and and_1 (and_1_out, NQ, T);
  and and_2 (and_2_out, T, Q);
  not not_1 (not_1_out, C);
  RS_Trigger rs_trigger_1 (.R(and_1_out), .C(C), .S(and_2_out), .Q(rs_trigger_1_q), .NQ(rs_trigger_1_nq));
  RS_Trigger rs_trigger_2 (.R(rs_trigger_1_q), .C(not_1_out), .S(rs_trigger_1_nq), .Q(Q), .NQ(NQ));
endmodule

module T_Trigger_2 (
  input  T,
  input  C,
  output Q
);

  wire and_1_out, d_trigger_1_q, d_trigger_2_nq, not_1_out;

  and and_1 (and_1_out, T, C);
  not not_1 (not_1_out, and_1_out);
  D_Trigger d_trigger_1 (.D(d_trigger_2_nq), .C(and_1_out), .Q(d_trigger_1_q));  // open: NQ
  D_Trigger d_trigger_2 (.D(d_trigger_1_q), .C(not_1_out), .Q(Q), .NQ(d_trigger_2_nq));
endmodule
