// Logisim project lfsr.circ as structural Verilog: 3 circuits, main circuit main
module main (
  input  C,
  input  D,
  input  I,
  input  A0,
  input  A1,
  input  A2,
  input  A3,
  input  A4,
  input  A5,
  input  A6,
  input  A7,
  input  A8,
  input  A9,
  input  A10,
  input  A11,
  input  A12,
  input  A13,
  input  A14,
  input  A15,
  output out_20,
  output out_21,
  output out_22,
  output out_23,
  output out_24,
  output out_25,
  output out_26,
  output out_27,
  output out_28,
  output out_29,
  output out_30,
  output out_31,
  output out_32,
  output out_33,
  output out_34,
  output out_35
);

  wire and_1_out, and_2_out, and_3_out, and_4_out, and_5_out, and_6_out, and_7_out, and_8_out, and_9_out,
       and_10_out, and_11_out, and_12_out, and_13_out, and_14_out, and_15_out, and_16_out, or_1_out,
       or_2_out, or_3_out, or_4_out, or_5_out, or_6_out, or_7_out, or_8_out, or_9_out, or_10_out, or_11_out,
       or_12_out, or_13_out, or_14_out, or_15_out, or_16_out, xor_1_out, xor_2_out;

  xor xor_1 (xor_1_out, out_27, out_35);
  ExactlyOne xor_2 (.out(xor_2_out), .in0(xor_1_out), .in1(D), .in2(out_20));
  or or_1 (or_1_out, out_27, and_9_out);
  or or_2 (or_2_out, xor_2_out, and_1_out);
  and and_1 (and_1_out, I, A0);
  and and_2 (and_2_out, I, A1);
  and and_3 (and_3_out, I, A2);
  and and_4 (and_4_out, I, A3);
  and and_5 (and_5_out, I, A4);
  and and_6 (and_6_out, I, A5);
  and and_7 (and_7_out, I, A6);
  and and_8 (and_8_out, I, A7);
  and and_9 (and_9_out, I, A8);
  and and_10 (and_10_out, I, A9);
  and and_11 (and_11_out, I, A10);
  and and_12 (and_12_out, I, A11);
  and and_13 (and_13_out, I, A12);
  and and_14 (and_14_out, I, A13);
  and and_15 (and_15_out, I, A14);
  and and_16 (and_16_out, I, A15);
  D_Trigger_Front d_trigger_front_1 (.D(or_2_out), .C(C), .Q(out_20));  // open: NQ
  D_Trigger_Front d_trigger_front_2 (.D(or_1_out), .C(C), .Q(out_28));  // open: NQ
  or or_3 (or_3_out, out_20, and_2_out);
  or or_4 (or_4_out, and_10_out, out_28);
  D_Trigger_Front d_trigger_front_3 (.D(or_3_out), .C(C), .Q(out_21));  // open: NQ
  D_Trigger_Front d_trigger_front_4 (.D(or_4_out), .C(C), .Q(out_29));  // open: NQ
  or or_5 (or_5_out, out_21, and_3_out);
  or or_6 (or_6_out, out_29, and_11_out);
  D_Trigger_Front d_trigger_front_5 (.D(or_5_out), .C(C), .Q(out_22));  // open: NQ
  D_Trigger_Front d_trigger_front_6 (.D(or_6_out), .C(C), .Q(out_30));  // open: NQ
  or or_7 (or_7_out, out_22, and_4_out);
  or or_8 (or_8_out, out_30, and_12_out);
  or or_9 (or_9_out, out_23, and_5_out);
  D_Trigger_Front d_trigger_front_7 (.D(or_7_out), .C(C), .Q(out_23));  // open: NQ
  D_Trigger_Front d_trigger_front_8 (.D(or_8_out), .C(C), .Q(out_31));  // open: NQ
  or or_10 (or_10_out, out_31, and_13_out);
  or or_11 (or_11_out, out_24, and_6_out);
  D_Trigger_Front d_trigger_front_9 (.D(or_9_out), .C(C), .Q(out_24));  // open: NQ
  D_Trigger_Front d_trigger_front_10 (.D(or_10_out), .C(C), .Q(out_32));  // open: NQ
  or or_12 (or_12_out, out_32, and_14_out);
  or or_13 (or_13_out, out_25, and_7_out);
  D_Trigger_Front d_trigger_front_11 (.D(or_11_out), .C(C), .Q(out_25));  // open: NQ
  D_Trigger_Front d_trigger_front_12 (.D(or_12_out), .C(C), .Q(out_33));  // open: NQ
  or or_14 (or_14_out, out_33, and_15_out);
  D_Trigger_Front d_trigger_front_13 (.D(or_13_out), .C(C), .Q(out_26));  // open: NQ
  D_Trigger_Front d_trigger_front_14 (.D(or_14_out), .C(C), .Q(out_34));  // open: NQ
  buf or_15 (or_15_out, out_26);  // OR_Gate
  or or_16 (or_16_out, out_34, and_16_out);
  D_Trigger_Front d_trigger_front_15 (.D(or_15_out), .C(C), .Q(out_27));  // open: NQ
  D_Trigger_Front d_trigger_front_16 (.D(or_16_out), .C(C), .Q(out_35));  // open: NQ
endmodule

module D_Trigger (
  input  D,
  input  C,
  output Q,
  output NQ
);

  wire nand_1_out, nand_2_out, nand_4_out, por_1_out;

  nand nand_1 (nand_1_out, D, C);
  nand nand_2 (nand_2_out, nand_1_out, C);
  nand nand_3 (Q, nand_1_out, NQ);
  nand nand_4 (nand_4_out, Q, nand_2_out);
  POR por_1 (.out(por_1_out));
  or or_1 (NQ, nand_4_out, por_1_out);
endmodule

module D_Trigger_Front (
  input  D,
  input  C,
  output Q,
  output NQ
);

  wire d_trigger_1_q, not_1_out;

  not not_1 (not_1_out, C);
  D_Trigger d_trigger_1 (.D(D), .C(C), .Q(d_trigger_1_q));  // open: NQ
  D_Trigger d_trigger_2 (.D(d_trigger_1_q), .C(not_1_out), .Q(Q), .NQ(NQ));
endmodule
